# Fritzing sketch TomatoDisplaySMD (saved by Fritzing 0.9.1b)
circuit board: 5.42097cm x 2.70621cm
breadboards: 1

parts:
  LED = 7-SEGMENT-4DIGIT [package=7-segment-4digit-luckylight]
  IC2 = 74HC595 SMD [package="SO16 [SMD]"]
  IC1 = 74HC595 SMD [package="SO16 [SMD]"]
  R2 = Resistor [tolerance=±5% resistance=1k package="0603 [SMD]"]
  R6 = Resistor [tolerance=±5% resistance=1k package="0603 [SMD]"]
  R1 = Resistor [tolerance=±5% resistance=1k package="0603 [SMD]"]
  R7 = Resistor [tolerance=±5% resistance=1k package="0603 [SMD]"]
  R4 = Resistor [tolerance=±5% resistance=1k package="0603 [SMD]"]
  R8 = Resistor [tolerance=±5% resistance=1k package="0603 [SMD]"]
  R3 = Resistor [tolerance=±5% resistance=1k package="0603 [SMD]"]
  R5 = Resistor [tolerance=±5% resistance=1k package="0603 [SMD]"]
  R9 = Resistor [tolerance=±5% resistance=1k package="0603 [SMD]"]
  JP1 = FTDI_BASIC [package=ftdi_basic]

nets:
  N1: LED.1, R3.Pin_0
  N2: LED.2, R2.Pin_0
  N3: LED.3, R9.Pin_0
  N4: LED.4, R6.Pin_0
  N5: LED.5, R1.Pin_0
  N6: LED.6, IC2.Q2
  N7: LED.7, IC2.Q1
  N8: LED.8, R5.Pin_1
  N9: LED.9, R8.Pin_1
  N10: LED.10, IC2.Q5
  N11: LED.11, IC1.Q4
  N12: LED.12, R4.Pin_1
  N13: LED.13, R7.Pin_1
  N14: LED.14, IC1.Q1
  N15: IC2.Q3, R1.Pin_1
  N16: IC2.Q4, R6.Pin_1
  N17: IC2.Q6, R8.Pin_0
  N18: IC2.Q7, R5.Pin_0
  GND: IC2.GND, IC1.GND, JP1.4
  N19: IC2.Q7', IC1.DS
  VCC: IC2.MR, IC2.VCC, IC1.MR, IC1.VCC, JP1.6
  N20: IC2.SH_CP, IC1.SH_CP, JP1.2
  N21: IC2.ST_CP, IC1.ST_CP, JP1.3
  N22: IC2.OE, IC1.OE, JP1.1
  N23: IC2.DS, JP1.5
  N24: IC1.Q2, R7.Pin_0
  N25: IC1.Q3, R4.Pin_0
  N26: IC1.Q5, R9.Pin_1
  N27: IC1.Q6, R2.Pin_1
  N28: IC1.Q7, R3.Pin_1

notes:
  1
  TomatoDisplay rev. A

custom parts:
  7-SEGMENT-4DIGIT: Luckylight 4 digit 7 segment LED display KW4-56NCLB-P
